# Fritzing sketch CtrlAccesPiscinePouldu (saved by Fritzing 1.0.4)
breadboards: 1

parts:
  Composant1 = Arduino Mega 2560 (Rev3)
  Composant2 = Arduino Ethernet Shield (Rev3)  # not connected
  Mod1 = Raspberry Pi 4B
  ZS-042_RTC1 = ZS-042 RTC Module
  M1 = ELECTROCOOKIE Uno Terminal Block Shield Kit  # not connected
  T1 = MDR-60-5 - Power Supply 60W 5V 10A [part_number=MDR-60-5]  # not connected
  U1 = 2-Channel 5v Relay Shield [package=relay-2ch5v10a]  # not connected
  A1 = terminal block grey  # not connected
  Rly1 = Finder55.34 [part_number="finder relay 55.34" package="socket 94.14"]  # not connected

nets:
  N1: Composant1.A5, Mod1.GPIO15
  N2: Composant1.D21/SCL, ZS-042_RTC1.SCL
  N3: Composant1.D20/SDA, ZS-042_RTC1.SDA
  3V3: Composant1.3V3, ZS-042_RTC1.VCC
  GND: Composant1.GND, ZS-042_RTC1.GND

custom parts:
  ELECTROCOOKIE Uno Terminal Block Shield Kit: ELECTROCOOKIE Uno Terminal Block Shield Kit, Compatible for Arduino Uno R3, Push-in Simple Spring Connector Expansion PCB Module.
  2-Channel 5v Relay Shield: 2 Channel 5v Relay Shield w. 2x SPD-06VDC-SD-C
  terminal block grey: terminal block grey.
  Finder55.34: Finder 55.34 4 pole double throw relay, mounted in a Finder 94.14 relay socket (pcb view).
